// Logisim project experiment1.circ as structural Verilog: 1 circuit, main circuit main
module main (
);

  wire and_1_out, and_2_out, and_3_out, and_4_out, and_5_out, and_6_out, and_7_out, and_8_out, i0_3_out,
       i0_5_out, i0_out, i1_2_out, i1_3_out, i1_5_out, i1_out, i2_2_out, i2_3_out, i2_5_out, i2_out,
       i3_2_out, i3_3_out, i3_5_out, i3_out, i4_2_out, i4_3_out, i4_5_out, i4_out, i5_2_out, i5_3_out,
       i5_5_out, i5_out, i6_2_out, i6_3_out, i6_5_out, i6_out, i7_2_out, i7_3_out, i7_5_out, i7_out,
       multiplexer_2_out, multiplexer_3_out, multiplexer_4_out, multiplexer_5_out, multiplexer_6_out,
       multiplexer_7_out, multiplexer_8_out, not_1_out, not_2_out, not_3_out, or_1_out, or_2_out, or_3_out,
       or_4_out, s0_2_out, s0_out, s1_2_out, s1_out, s2_2_out, s2_out;
  wire [2:0] priority_encoder_1_gs, undriven;
  wire [7:0] i0_4_out, i1_4_out, i2_4_out, i3_4_out, i4_4_out, i5_4_out, i6_4_out, i7_4_out,
       multiplexer_1_out;

  Button i0 (.out(i0_out));
  Button i1 (.out(i1_out));
  Button i2 (.out(i2_out));
  Button i3 (.out(i3_out));
  Button i4 (.out(i4_out));
  Button i5 (.out(i5_out));
  Button i6 (.out(i6_out));
  Button i7 (.out(i7_out));
  Button s0 (.out(s0_out));
  Button i7_2 (.out(i7_2_out));
  Button s1 (.out(s1_out));
  not not_1 (not_1_out, s0_out);
  Button i6_2 (.out(i6_2_out));
  not not_2 (not_2_out, s1_out);
  Button s2 (.out(s2_out));
  Button i5_2 (.out(i5_2_out));
  not not_3 (not_3_out, s2_out);
  Button i4_2 (.out(i4_2_out));
  Button i3_2 (.out(i3_2_out));
  and and_1 (and_1_out, not_1_out, i0_out, not_2_out, not_3_out);
  and and_2 (and_2_out, not_1_out, i1_out, not_2_out, s2_out);
  and and_3 (and_3_out, not_1_out, i2_out, s1_out, not_3_out);
  and and_4 (and_4_out, not_1_out, i3_out, s1_out, s2_out);
  and and_5 (and_5_out, s0_out, i4_out, not_2_out, not_3_out);
  and and_6 (and_6_out, s0_out, i5_out, not_2_out, s2_out);
  and and_7 (and_7_out, s0_out, i6_out, s1_out, not_3_out);
  and and_8 (and_8_out, s0_out, i7_out, s1_out, s2_out);
  Button i2_2 (.out(i2_2_out));
  Button i1_2 (.out(i1_2_out));
  Button i0_2 ();  // open: out
  or or_1 (or_1_out, and_1_out, and_2_out, and_3_out, and_4_out, and_5_out, and_6_out, and_7_out, and_8_out);
  or or_2 (or_2_out, i1_2_out, i3_2_out, i5_2_out, i7_2_out);
  LED led_1 (.in(or_2_out));
  LED led_2 (.in(or_3_out));
  or or_3 (or_3_out, i2_2_out, i3_2_out, i6_2_out, i7_2_out);
  LED led_3 (.in(or_4_out));
  or or_4 (or_4_out, i4_2_out, i5_2_out, i6_2_out, i7_2_out);
  LED led_4 (.in(or_1_out));
  Button i0_3 (.out(i0_3_out));
  Button i1_3 (.out(i1_3_out));
  Button i2_3 (.out(i2_3_out));
  Button i3_3 (.out(i3_3_out));
  Button i4_3 (.out(i4_3_out));
  Button i5_3 (.out(i5_3_out));
  Button i6_3 (.out(i6_3_out));
  Button i7_3 (.out(i7_3_out));
  Button s0_2 (.out(s0_2_out));
  Button i0_4 (.out(i0_4_out[0]));
  Button i1_4 (.out(i1_4_out[0]));
  Button i2_4 (.out(i2_4_out[0]));
  Button i3_4 (.out(i3_4_out[0]));
  Button i4_4 (.out(i4_4_out[0]));
  Button i5_4 (.out(i5_4_out[0]));
  Button i6_4 (.out(i6_4_out[0]));
  Button i7_4 (.out(i7_4_out[0]));
  Priority_Encoder priority_encoder_1 (
    .in0(i0_3_out), .in1(i1_3_out), .in2(i2_3_out), .in3(i3_3_out), .in4(i4_3_out), .in5(i5_3_out),
    .in6(i6_3_out), .in7(i7_3_out), .gs(priority_encoder_1_gs[0]));  // open: out, en_in, en_out
  Button i0_5 (.out(i0_5_out));
  Button i1_5 (.out(i1_5_out));
  Button i2_5 (.out(i2_5_out));
  Button i3_5 (.out(i3_5_out));
  Button i4_5 (.out(i4_5_out));
  Button i5_5 (.out(i5_5_out));
  Button i6_5 (.out(i6_5_out));
  Button i7_5 (.out(i7_5_out));
  Multiplexer #(.select(3), .width(8)) multiplexer_1 (
    .in0(i0_4_out), .in1(i1_4_out), .in2(i2_4_out), .in3(i3_4_out), .in4(i4_4_out), .in5(i5_4_out),
    .in6(i6_4_out), .in7(i7_4_out), .out(multiplexer_1_out), .en(undriven[0]));  // open: sel
  LED led_5 (.in(priority_encoder_1_gs[0]));
  LED led_6 (.in(priority_encoder_1_gs[1]));
  LED led_7 (.in(priority_encoder_1_gs[2]));
  LED led_8 (.in(multiplexer_1_out[0]));
  Button button_1 ();  // open: out
  Button button_2 ();  // open: out
  Button button_3 ();  // open: out
  Button s1_2 (.out(s1_2_out));
  Multiplexer multiplexer_2 (.in0(i0_5_out), .in1(i1_5_out), .out(multiplexer_2_out), .sel(s0_2_out));  // open: en
  Multiplexer multiplexer_3 (.in0(i2_5_out), .in1(i3_5_out), .out(multiplexer_3_out), .sel(s0_2_out));  // open: en
  Multiplexer multiplexer_4 (.in0(i4_5_out), .in1(i5_5_out), .out(multiplexer_4_out), .sel(s0_2_out));  // open: en
  Multiplexer multiplexer_5 (.in0(i6_5_out), .in1(i7_5_out), .out(multiplexer_5_out), .sel(s0_2_out));  // open: en
  Multiplexer multiplexer_6 (
    .in0(multiplexer_2_out), .in1(multiplexer_3_out), .out(multiplexer_6_out), .sel(s1_2_out));  // open: en
  Multiplexer multiplexer_7 (
    .in0(multiplexer_4_out), .in1(multiplexer_5_out), .out(multiplexer_7_out), .sel(s1_2_out));  // open: en
  Button s2_2 (.out(s2_2_out));
  Multiplexer multiplexer_8 (
    .in0(multiplexer_6_out), .in1(multiplexer_7_out), .out(multiplexer_8_out), .sel(s2_2_out));  // open: en
  LED led_9 (.in(multiplexer_8_out));
  // Pins of 1 and 3 bits meet at undriven
  // Pins of 1 and 8 bits meet at i7_4_out
  // Pins of 1 and 8 bits meet at i4_4_out
  // Pins of 1 and 8 bits meet at i0_4_out
  // Pins of 1 and 8 bits meet at i2_4_out
  // Pins of 1 and 8 bits meet at i1_4_out
  // Pins of 1 and 8 bits meet at i3_4_out
  // Pins of 1 and 8 bits meet at i5_4_out
  // Pins of 1 and 8 bits meet at i6_4_out
  // Pins of 1 and 8 bits meet at multiplexer_1_out
  // Pins of 1 and 3 bits meet at priority_encoder_1_gs
endmodule
