// Logisim project experiment2.circ as structural Verilog: 1 circuit, main circuit main
module main (
  input  in_1,
  input  in_2,
  input  in_3,
  input  in_4,
  input  in_5,
  input  in_6,
  input  in_7,
  input  in_8,
  input  in_9
);

  wire and_1_out, and_2_out, and_3_out, and_4_out, and_5_out, and_6_out, and_7_out, and_8_out, and_9_out,
       and_10_out, and_11_out, and_12_out, and_13_out, and_14_out, and_15_out, and_16_out, and_17_out,
       and_18_out, and_19_out, and_20_out, and_21_out, and_22_out, and_23_out, and_24_out, and_25_out,
       and_26_out, and_27_out, and_28_out, not_1_out, not_2_out, not_3_out, not_4_out, not_5_out, not_6_out,
       not_7_out, not_8_out, not_9_out, not_10_out, not_11_out, not_12_out, or_1_out, or_2_out, or_3_out,
       or_4_out, or_5_out, or_6_out, or_7_out, or_8_out;

  not not_1 (not_1_out, in_1);
  not not_2 (not_2_out, in_2);
  not not_3 (not_3_out, in_3);
  and and_1 (and_1_out, in_3, in_2);
  and and_2 (and_2_out, in_3, in_1);
  and and_3 (and_3_out, in_1, in_2);
  and and_4 (and_4_out, not_2_out, not_3_out, in_1);
  and and_5 (and_5_out, not_2_out, in_3, not_1_out);
  and and_6 (and_6_out, in_2, not_3_out, not_1_out);
  and and_7 (and_7_out, in_2, in_3, in_1);
  or or_1 (or_1_out, and_1_out, and_2_out, and_3_out);
  or or_2 (or_2_out, and_4_out, and_5_out, and_6_out, and_7_out);
  not not_4 (not_4_out, or_1_out);
  LED led_1 (.in(or_8_out));
  LED led_2 (.in(or_6_out));
  LED led_3 (.in(or_4_out));
  not not_5 (not_5_out, in_4);
  LED led_4 (.in(or_2_out));
  not not_6 (not_6_out, in_5);
  and and_8 (and_8_out, in_5, in_4);
  and and_9 (and_9_out, in_5, or_1_out);
  and and_10 (and_10_out, or_1_out, in_4);
  and and_11 (and_11_out, not_5_out, not_6_out, or_1_out);
  and and_12 (and_12_out, not_5_out, in_5, not_4_out);
  and and_13 (and_13_out, in_4, not_6_out, not_4_out);
  and and_14 (and_14_out, in_4, in_5, or_1_out);
  or or_3 (or_3_out, and_8_out, and_9_out, and_10_out);
  or or_4 (or_4_out, and_11_out, and_12_out, and_13_out, and_14_out);
  not not_7 (not_7_out, or_3_out);
  not not_8 (not_8_out, in_6);
  not not_9 (not_9_out, in_7);
  and and_15 (and_15_out, in_7, in_6);
  and and_16 (and_16_out, in_7, or_3_out);
  and and_17 (and_17_out, or_3_out, in_6);
  and and_18 (and_18_out, not_8_out, not_9_out, or_3_out);
  and and_19 (and_19_out, not_8_out, in_7, not_7_out);
  and and_20 (and_20_out, in_6, not_9_out, not_7_out);
  and and_21 (and_21_out, in_6, in_7, or_3_out);
  or or_5 (or_5_out, and_15_out, and_16_out, and_17_out);
  or or_6 (or_6_out, and_18_out, and_19_out, and_20_out, and_21_out);
  not not_10 (not_10_out, or_5_out);
  not not_11 (not_11_out, in_8);
  not not_12 (not_12_out, in_9);
  and and_22 (and_22_out, in_9, in_8);
  and and_23 (and_23_out, in_9, or_5_out);
  and and_24 (and_24_out, or_5_out, in_8);
  and and_25 (and_25_out, not_11_out, not_12_out, or_5_out);
  and and_26 (and_26_out, not_11_out, in_9, not_10_out);
  and and_27 (and_27_out, in_8, not_12_out, not_10_out);
  and and_28 (and_28_out, in_8, in_9, or_5_out);
  or or_7 (or_7_out, and_22_out, and_23_out, and_24_out);
  or or_8 (or_8_out, and_25_out, and_26_out, and_27_out, and_28_out);
  LED led_5 (.in(or_7_out));
endmodule
