// Logisim project experiment3.circ as structural Verilog: 1 circuit, main circuit main
module main (
  input  in_1,
  input  [7:0] in_2,
  input  in_3,
  input  in_4,
  output out_5
);

  wire clock_1_out, clock_2_out, d_ff_2_q, d_ff_5_q, d_ff_8_q, d_ff_10_q, d_ff_13_q, d_ff_14_q, d_ff_15_q,
       multiplexer_1_out, multiplexer_2_out, multiplexer_3_out, multiplexer_4_out, multiplexer_5_out,
       multiplexer_6_out, multiplexer_7_out, multiplexer_8_out;
  wire [7:0] d_ff_1_q;

  Clock clock_1 (.out(clock_1_out));
  Multiplexer #(.enable("false")) multiplexer_1 (.in0(in_3), .in1(in_2[7]), .out(multiplexer_1_out), .sel(in_4));
  Clock clock_2 (.out(clock_2_out));
  D_Flip_Flop d_ff_1 (.clk(clock_1_out), .D(in_1), .Q(d_ff_1_q[0]));  // open: Qn, preset, en, reset
  D_Flip_Flop d_ff_2 (.clk(clock_2_out), .D(multiplexer_1_out), .Q(d_ff_2_q));  // open: Qn, preset, en, reset
  D_Flip_Flop d_ff_3 (.clk(clock_1_out), .D(d_ff_1_q[0]), .Q(d_ff_1_q[1]));  // open: Qn, preset, en, reset
  Multiplexer #(.enable("false")) multiplexer_2 (.in0(d_ff_2_q), .in1(in_2[6]), .out(multiplexer_2_out), .sel(in_4));
  D_Flip_Flop d_ff_4 (.clk(clock_1_out), .D(d_ff_1_q[1]), .Q(d_ff_1_q[2]));  // open: Qn, preset, en, reset
  D_Flip_Flop d_ff_5 (.clk(clock_2_out), .D(multiplexer_2_out), .Q(d_ff_5_q));  // open: Qn, preset, en, reset
  D_Flip_Flop d_ff_6 (.clk(clock_1_out), .D(d_ff_1_q[2]), .Q(d_ff_1_q[3]));  // open: Qn, preset, en, reset
  Multiplexer #(.enable("false")) multiplexer_3 (.in0(d_ff_5_q), .in1(in_2[5]), .out(multiplexer_3_out), .sel(in_4));
  D_Flip_Flop d_ff_7 (.clk(clock_1_out), .D(d_ff_1_q[3]), .Q(d_ff_1_q[4]));  // open: Qn, preset, en, reset
  D_Flip_Flop d_ff_8 (.clk(clock_2_out), .D(multiplexer_3_out), .Q(d_ff_8_q));  // open: Qn, preset, en, reset
  D_Flip_Flop d_ff_9 (.clk(clock_1_out), .D(d_ff_1_q[4]), .Q(d_ff_1_q[5]));  // open: Qn, preset, en, reset
  D_Flip_Flop d_ff_10 (.clk(clock_2_out), .D(multiplexer_4_out), .Q(d_ff_10_q));  // open: Qn, preset, en, reset
  Multiplexer #(.enable("false")) multiplexer_4 (.in0(d_ff_8_q), .in1(in_2[4]), .out(multiplexer_4_out), .sel(in_4));
  D_Flip_Flop d_ff_11 (.clk(clock_1_out), .D(d_ff_1_q[5]), .Q(d_ff_1_q[6]));  // open: Qn, preset, en, reset
  Multiplexer #(.enable("false")) multiplexer_5 (.in0(d_ff_10_q), .in1(in_2[3]), .out(multiplexer_5_out), .sel(in_4));
  D_Flip_Flop d_ff_12 (.clk(clock_1_out), .D(d_ff_1_q[6]), .Q(d_ff_1_q[7]));  // open: Qn, preset, en, reset
  D_Flip_Flop d_ff_13 (.clk(clock_2_out), .D(multiplexer_5_out), .Q(d_ff_13_q));  // open: Qn, preset, en, reset
  // Probe on d_ff_1_q
  Multiplexer #(.enable("false")) multiplexer_6 (.in0(d_ff_13_q), .in1(in_2[2]), .out(multiplexer_6_out), .sel(in_4));
  D_Flip_Flop d_ff_14 (.clk(clock_2_out), .D(multiplexer_6_out), .Q(d_ff_14_q));  // open: Qn, preset, en, reset
  Multiplexer #(.enable("false")) multiplexer_7 (.in0(d_ff_14_q), .in1(in_2[1]), .out(multiplexer_7_out), .sel(in_4));
  D_Flip_Flop d_ff_15 (.clk(clock_2_out), .D(multiplexer_7_out), .Q(d_ff_15_q));  // open: Qn, preset, en, reset
  D_Flip_Flop d_ff_16 (.clk(clock_2_out), .D(multiplexer_8_out), .Q(out_5));  // open: Qn, preset, en, reset
  Multiplexer #(.enable("false")) multiplexer_8 (.in0(d_ff_15_q), .in1(in_2[0]), .out(multiplexer_8_out), .sel(in_4));
endmodule
